# Fritzing sketch ATMega_328P_ISP-Adapter_v10_Masse (saved by Fritzing 1.0.1rc)
circuit board: 4.6cm x 5.55cm
breadboards: 1

parts:
  328P = ATmega328 [package=tqfp]
  ISP = AVR ISP 6 Pin [package=2x3]
  Debug = Molex 6 Pin Header

nets:
  GND: 328P.GND, ISP.6, Debug.GND
  VCC: 328P.VCC, ISP.2, Debug.VCC
  N1: 328P.PB3(MOSI_OC2), ISP.4, Debug.MISO
  N2: 328P.PB4(MISO), ISP.1, Debug.RST
  N3: 328P.PB5(SCK), ISP.3, Debug.MOSI
  N4: 328P.PC6(_RESET), ISP.5, Debug.SCK

notes:
  32
  1
  2
  3
  4
  5
  6
  7
  8
  9
  10
  11
  12
  13
  14
  15
  16
  31
  30
  29
  28
  27
  26
  25
  24
  23
  22
  21
  20
  19
  18
  17
  VCC
  GND
  TXD
  RXD
  DTR
  328 Prog Adpt AM V1.0

custom parts:
  Molex 6 Pin Header: Board Connector 501331
